# Fritzing sketch potentiometer (saved by Fritzing 0.9.3b)
breadboards: 1

parts:
  R1 = Rotary Potentiometer (Large) [maximum_resistance=10kΩ package=THT]
  J1 = female pin header, 6 pins [form="♀ (female)"]

nets:
  N1: R1.leg1, J1.pin5
  N2: R1.wiper, J1.pin1
  N3: R1.leg2, J1.pin6
